// Logisim project 2207065.circ as structural Verilog: 30 circuits, main circuit main
module main (
);


  // Notes on the sheet:
  //   2207065
  //   Nurul Absar Shadik
endmodule

// AND
module _19_BIT_AND (
  input  [18:0] A,
  input  [18:0] B,
  output [18:0] A_and_B
);

  assign A_and_B = A & B;  // AND_Gate and_1, 19 bits wide

  // Notes on the sheet:
  //   Nurul Absar Shadik
endmodule

// OR
module _19_BIT_OR (
  input  [18:0] A,
  input  [18:0] B,
  output [18:0] A_OR_B
);

  assign A_OR_B = A | B;  // OR_Gate or_1, 19 bits wide

  // Notes on the sheet:
  //   Nurul Absar Shadik
endmodule

module _1_bit_adder (
  input  Cin,
  input  A,
  input  B,
  output Sum,
  output Cout
);

  wire and_1_out, and_2_out, xor_1_out;

  and and_1 (and_1_out, A, B);
  xor xor_1 (xor_1_out, A, B);
  xor xor_2 (Sum, Cin, xor_1_out);
  and and_2 (and_2_out, Cin, xor_1_out);
  or or_1 (Cout, and_2_out, and_1_out);

  // Notes on the sheet:
  //   Nurul Absar Shadik
endmodule

module _2_BIT_CLA (
  input  Cin,
  input  P0,
  input  P1,
  input  G0,
  input  G1,
  output C0,
  output C1
);

  wire and_1_out, and_2_out, and_3_out;

  and and_1 (and_1_out, Cin, P0);
  and and_2 (and_2_out, and_1_out, P1);
  and and_3 (and_3_out, G0, P1);
  or or_1 (C0, and_1_out, G0);
  or or_2 (C1, and_2_out, G1, and_3_out);

  // Notes on the sheet:
  //   Nurul Absar Shadik
endmodule

module _3_BIT_CLA (
  input  Cin,
  input  P0,
  input  P1,
  input  G0,
  input  G1,
  input  P2,
  input  G2,
  output C0,
  output C1,
  output C2
);

  wire and_1_out, and_2_out, and_3_out, and_4_out, and_5_out, and_6_out;

  and and_1 (and_1_out, Cin, P0);
  and and_2 (and_2_out, and_1_out, P1);
  and and_3 (and_3_out, G0, P1);
  and and_4 (and_4_out, and_2_out, P2);
  and and_5 (and_5_out, G0, P1, P2);
  and and_6 (and_6_out, G1, P2);
  or or_1 (C0, and_1_out, G0);
  or or_2 (C1, and_2_out, G1, and_3_out);
  or or_3 (C2, and_4_out, and_5_out, and_6_out, G2);

  // Notes on the sheet:
  //   Nurul Absar Shadik
endmodule

module _4_BIT_CLA (
  input  Cin,
  input  P0,
  input  P1,
  input  G0,
  input  G1,
  input  P2,
  input  G2,
  input  P3,
  input  G3,
  output C0,
  output C1,
  output C2,
  output C3
);

  wire and_1_out, and_2_out, and_3_out, and_4_out, and_5_out, and_6_out, and_7_out, and_8_out, and_9_out,
       and_10_out;

  and and_1 (and_1_out, P3, G2);
  and and_2 (and_2_out, and_9_out, P3);
  and and_3 (and_3_out, and_10_out, P3);
  and and_4 (and_4_out, Cin, P0);
  and and_5 (and_5_out, and_4_out, P1);
  and and_6 (and_6_out, G0, P1);
  and and_7 (and_7_out, and_8_out, P3);
  and and_8 (and_8_out, and_5_out, P2);
  and and_9 (and_9_out, G0, P1, P2);
  and and_10 (and_10_out, G1, P2);
  or or_1 (C0, and_4_out, G0);
  or or_2 (C1, and_5_out, G1, and_6_out);
  or or_3 (C2, and_8_out, and_9_out, and_10_out, G2);
  or or_4 (C3, and_7_out, and_2_out, and_3_out, and_1_out, G3);

  // Notes on the sheet:
  //   Nurul Absar Shadik
endmodule

module _2_BIT_ADDER (
  input  Cin,
  input  [1:0] A,
  input  [1:0] B,
  output [1:0] sum,
  output carry
);

  wire and_1_out, and_2_out, n2_bit_cla_1_c0, xor_1_out, xor_2_out;

  xor xor_1 (xor_1_out, A[0], B[0]);
  and and_1 (and_1_out, A[0], B[0]);
  xor xor_2 (xor_2_out, A[1], B[1]);
  and and_2 (and_2_out, A[1], B[1]);
  _2_BIT_CLA u_2_bit_cla_1 (
    .Cin(Cin), .P0(xor_1_out), .P1(xor_2_out), .G0(and_1_out), .G1(and_2_out), .C0(n2_bit_cla_1_c0),
    .C1(carry));
  _1_bit_adder u_1_bit_adder_1 (.Cin(Cin), .A(A[0]), .B(B[0]), .Sum(sum[0]));  // open: Cout
  _1_bit_adder u_1_bit_adder_2 (.Cin(n2_bit_cla_1_c0), .A(A[1]), .B(B[1]), .Sum(sum[1]));  // open: Cout

  // Notes on the sheet:
  //   Nurul Absar Shadik
endmodule

module _4_BIT_ADDER (
  input  Cin,
  input  [3:0] A,
  input  [3:0] B,
  output [3:0] SUM,
  output Carry
);

  wire and_1_out, and_2_out, and_3_out, and_4_out, n4_bit_cla_1_c1, xor_1_out, xor_2_out, xor_3_out,
       xor_4_out;

  xor xor_1 (xor_1_out, A[0], B[0]);
  xor xor_2 (xor_2_out, A[1], B[1]);
  xor xor_3 (xor_3_out, A[2], B[2]);
  xor xor_4 (xor_4_out, A[3], B[3]);
  and and_1 (and_1_out, A[0], B[0]);
  and and_2 (and_2_out, A[1], B[1]);
  and and_3 (and_3_out, A[2], B[2]);
  and and_4 (and_4_out, A[3], B[3]);
  _4_BIT_CLA u_4_bit_cla_1 (
    .Cin(Cin), .P0(xor_1_out), .P1(xor_2_out), .G0(and_1_out), .G1(and_2_out), .P2(xor_3_out),
    .G2(and_3_out), .P3(xor_4_out), .G3(and_4_out), .C1(n4_bit_cla_1_c1), .C3(Carry));  // open: C0, C2
  _2_BIT_ADDER u_2_bit_adder_1 (.Cin(Cin), .A(A[1:0]), .B(B[1:0]), .sum(SUM[1:0]));  // open: carry
  _2_BIT_ADDER u_2_bit_adder_2 (.Cin(n4_bit_cla_1_c1), .A(A[3:2]), .B(B[3:2]), .sum(SUM[3:2]));  // open: carry

  // Notes on the sheet:
  //   Nurul Absar Shadik
endmodule

module _3_BIT_ADDER (
  input  CIN,
  input  [2:0] A,
  input  [2:0] B,
  output [2:0] sum,
  output carry
);

  wire and_1_out, and_2_out, and_3_out, n3_bit_cla_1_c1, xor_1_out, xor_2_out, xor_3_out;

  xor xor_1 (xor_1_out, A[0], B[0]);
  xor xor_2 (xor_2_out, A[1], B[1]);
  xor xor_3 (xor_3_out, A[2], B[2]);
  and and_1 (and_1_out, A[0], B[0]);
  and and_2 (and_2_out, A[1], B[1]);
  and and_3 (and_3_out, A[2], B[2]);
  _3_BIT_CLA u_3_bit_cla_1 (
    .Cin(CIN), .P0(xor_1_out), .P1(xor_2_out), .G0(and_1_out), .G1(and_2_out), .P2(xor_3_out),
    .G2(and_3_out), .C1(n3_bit_cla_1_c1), .C2(carry));  // open: C0
  _2_BIT_ADDER u_2_bit_adder_1 (.Cin(CIN), .A(A[1:0]), .B(B[1:0]), .sum(sum[1:0]));  // open: carry
  _1_bit_adder u_1_bit_adder_1 (.Cin(n3_bit_cla_1_c1), .A(A[2]), .B(B[2]), .Sum(sum[2]));  // open: Cout

  // Notes on the sheet:
  //   Nurul Absar Shadik
endmodule

module _8_BIT_ADDER (
  input  CIN,
  input  [7:0] A,
  input  [7:0] B,
  output [7:0] SUM,
  output COUT
);

  wire n4_bit_adder_1_carry;

  _4_BIT_ADDER u_4_bit_adder_1 (.Cin(CIN), .A(A[3:0]), .B(B[3:0]), .SUM(SUM[3:0]), .Carry(n4_bit_adder_1_carry));
  _4_BIT_ADDER u_4_bit_adder_2 (.Cin(n4_bit_adder_1_carry), .A(A[7:4]), .B(B[7:4]), .SUM(SUM[7:4]), .Carry(COUT));

  // Notes on the sheet:
  //   Nurul Absar Shadik
endmodule

// AS
module _19_bit_Adder_and_subtractor (
  input  Cin,
  input  [18:0] A,
  input  [18:0] B,
  output [18:0] Sum,
  output Carry,
  output Overflow
);

  wire and_1_out, and_2_out, msb_extract_1_out_2, msb_extract_2_out_2, msb_extract_3_out_2,
       n8_bit_adder_1_cout, n8_bit_adder_2_cout, not_1_out, not_2_out, not_3_out;
  wire [18:0] bit_extender_1_out, xor_1_out;

  assign bit_extender_1_out = {{18{Cin}}, Cin};  // Bit_Extender bit_extender_1
  assign xor_1_out = bit_extender_1_out ^ B;  // XOR_Gate xor_1, 19 bits wide
  MSB_EXTRACT msb_extract_1 (.in_1(A), .out_2(msb_extract_1_out_2));
  MSB_EXTRACT msb_extract_2 (.in_1(xor_1_out), .out_2(msb_extract_2_out_2));
  not not_1 (not_1_out, msb_extract_1_out_2);
  MSB_EXTRACT msb_extract_3 (.in_1(Sum), .out_2(msb_extract_3_out_2));
  not not_2 (not_2_out, msb_extract_2_out_2);
  not not_3 (not_3_out, msb_extract_3_out_2);
  and and_1 (and_1_out, msb_extract_3_out_2, not_2_out, not_1_out);
  and and_2 (and_2_out, msb_extract_1_out_2, msb_extract_2_out_2, not_3_out);
  _8_BIT_ADDER u_8_bit_adder_1 (.CIN(Cin), .A(A[7:0]), .B(xor_1_out[7:0]), .SUM(Sum[7:0]), .COUT(n8_bit_adder_1_cout));
  _8_BIT_ADDER u_8_bit_adder_2 (
    .CIN(n8_bit_adder_1_cout), .A(A[15:8]), .B(xor_1_out[15:8]), .SUM(Sum[15:8]), .COUT(n8_bit_adder_2_cout));
  _3_BIT_ADDER u_3_bit_adder_1 (
    .CIN(n8_bit_adder_2_cout), .A(A[18:16]), .B(xor_1_out[18:16]), .sum(Sum[18:16]), .carry(Carry));
  or or_1 (Overflow, and_1_out, and_2_out);

  // Notes on the sheet:
  //   Nurul Absar Shadik
endmodule

module MSB_EXTRACT (
  input  [18:0] in_1,
  output out_2
);


  assign out_2 = in_1[18];

  // Notes on the sheet:
  //   Nurul Absar Shadik
endmodule

module Zero_check (
  input  [18:0] in_1,
  output out_2
);

  wire or_1_out;

  or or_1 (or_1_out, in_1[0], in_1[1], in_1[2], in_1[3], in_1[4], in_1[5], in_1[6], in_1[7], in_1[8], in_1[9], in_1[10], in_1[11], in_1[12], in_1[13], in_1[14], in_1[15], in_1[16], in_1[17], in_1[18]);
  not not_1 (out_2, or_1_out);

  // Notes on the sheet:
  //   Nurul Absar Shadik
endmodule

module _2x1_MUX (
  input  S0,
  input  [18:0] in_2,
  input  [18:0] in_3,
  output [18:0] out_4
);

  wire [18:0] and_1_out, and_2_out, bit_extender_1_out, not_1_out;

  assign bit_extender_1_out = {{18{S0}}, S0};  // Bit_Extender bit_extender_1
  assign not_1_out = ~bit_extender_1_out;  // NOT_Gate not_1, 19 bits wide
  assign and_1_out = not_1_out & in_2;  // AND_Gate and_1, 19 bits wide
  assign and_2_out = in_3 & bit_extender_1_out;  // AND_Gate and_2, 19 bits wide
  assign out_4 = and_1_out | and_2_out;  // OR_Gate or_1, 19 bits wide

  // Notes on the sheet:
  //   Nurul Absar Shadik
endmodule

module _19_BIT_ALU (
  input  [1:0] Control,
  input  [18:0] A,
  input  [18:0] B,
  output [18:0] result
);

  wire and_1_out, and_2_out, msb_2_out_2, msb_out_2, n19_bit_adder_and_subtractor_1_carry,
       n19_bit_adder_and_subtractor_1_overflow;
  wire [18:0] n2x1_mux_1_out_4, n19_bit_adder_and_subtractor_1_sum, n19_bit_and_1_a_and_b,
       n19_bit_or_1_a_or_b;

  _19_BIT_AND u_19_bit_and_1 (.A(A), .B(B), .A_and_B(n19_bit_and_1_a_and_b));
  _19_BIT_OR u_19_bit_or_1 (.A(A), .B(B), .A_OR_B(n19_bit_or_1_a_or_b));
  _19_bit_Adder_and_subtractor u_19_bit_adder_and_subtractor_1 (
    .Cin(Control[0]), .A(A), .B(B), .Sum(n19_bit_adder_and_subtractor_1_sum),
    .Carry(n19_bit_adder_and_subtractor_1_carry), .Overflow(n19_bit_adder_and_subtractor_1_overflow));
  and and_1 (and_1_out, n19_bit_adder_and_subtractor_1_overflow, Control[1]);
  and and_2 (and_2_out, msb_out_2, Control[0], Control[1]);
  _2x1_MUX u_2x1_mux_1 (
    .S0(Control[0]), .in_2(n19_bit_or_1_a_or_b), .in_3(n19_bit_and_1_a_and_b), .out_4(n2x1_mux_1_out_4));
  _2x1_MUX _2x1_MUX (
    .S0(Control[1]), .in_2(n2x1_mux_1_out_4), .in_3(n19_bit_adder_and_subtractor_1_sum), .out_4(result));
  LED Negative (.in(and_2_out));
  LED Zero (.in(msb_2_out_2));
  LED Carry (.in(n19_bit_adder_and_subtractor_1_carry));
  LED Overflow (.in(and_1_out));
  MSB_EXTRACT msb (.in_1(result), .out_2(msb_out_2));
  Zero_check msb_2 (.in_1(result), .out_2(msb_2_out_2));

  // Notes on the sheet:
  //   2207065
  //   Nurul Absar Shadik
  //   operations
  //   00- OR
  //   01-AND
  //   10-ADDER
  //   11-Subtractor
endmodule

module State_equation (
  input  [1:0] Q,
  input  [2:0] T,
  input  C,
  output Da,
  output Db,
  output Dc
);

  wire and_1_out, and_2_out, and_3_out, and_4_out, and_5_out, or_4_out, or_5_out, Q0, Q1, Q2, Q3, T0, T1, T2,
       T3, T4, T5, T6, T7;

  Decoder #(.select(2), .enable("false")) decoder_1 (.out0(Q0), .out1(Q1), .out2(Q2), .out3(Q3), .sel(Q));
  Decoder #(.select(3), .enable("false")) decoder_2 (
    .out0(T0), .out1(T1), .out2(T2), .out3(T3), .out4(T4), .out5(T5), .out6(T6), .out7(T7), .sel(T));
  or or_1 (Da, T0, and_4_out, T3, T4, and_5_out, T7);
  or or_2 (Db, T1, and_1_out, T5, T6, T7);
  or or_3 (Dc, T5, and_2_out, T3, T4, T7, and_3_out);
  and and_1 (and_1_out, T2, Q2);
  and and_2 (and_2_out, T2, or_5_out);
  and and_3 (and_3_out, T6, C);
  and and_4 (and_4_out, T2, or_4_out);
  or or_4 (or_4_out, Q0, Q2, Q3);
  and and_5 (and_5_out, T6, C);
  or or_5 (or_5_out, Q0, Q1, Q3);

  // Notes on the sheet:
  //   Nurul Absar Shadik
endmodule

module Controller (
  input  CLK,
  input  RESET,
  input  Q0,
  input  Q_1,
  input  [4:0] count,
  output Ci_A_Q_1,
  output Load_M_Q_cnt,
  output LOAD_A,
  output C0,
  output C1,
  output Shr,
  output Dec_cnt
);

  wire nor_1_out, state_equation_1_da, state_equation_1_db, state_equation_1_dc, T0, T2, T4, T6, T7;
  wire [2:0] T;

  State_equation state_equation_1 (
    .Q({Q0, Q_1}), .T(T), .C(nor_1_out), .Da(state_equation_1_da), .Db(state_equation_1_db),
    .Dc(state_equation_1_dc));
  nor nor_1 (nor_1_out, count[0], count[1], count[2], count[3], count[4]);
  Decoder #(.select(3), .enable("false")) decoder_1 (
    .out0(T0), .out1(Ci_A_Q_1), .out2(T2), .out3(C0), .out4(T4), .out5(Dec_cnt), .out6(T6), .out7(T7), .sel(T));
  D_Flip_Flop d_ff_1 (.clk(CLK), .D(state_equation_1_da), .Q(T[0]), .reset(RESET));  // open: Qn, preset, en
  D_Flip_Flop d_ff_2 (.clk(CLK), .D(state_equation_1_db), .Q(T[1]), .reset(RESET));  // open: Qn, preset, en
  D_Flip_Flop d_ff_3 (.clk(CLK), .D(state_equation_1_dc), .Q(T[2]), .reset(RESET));  // open: Qn, preset, en
  or or_1 (LOAD_A, C0, T4);
  or or_2 (C1, T4, C0);

  assign Load_M_Q_cnt = Ci_A_Q_1;
  assign Shr = Dec_cnt;

  // Other names for the same wires on the sheet: T1 = Ci_A_Q_1; T3 = C0; T5 = Dec_cnt

  // Notes on the sheet:
  //   Nurul Absar Shadik
endmodule

module _2_s_complement (
  input  in_1,
  input  [18:0] in_2,
  output [18:0] out_3
);

  wire [17:0] not_1_out;
  wire [18:0] n19_bit_adder_and_subtractor_1_sum;

  not not_1 (not_1_out[0], in_2[0]);
  not not_2 (not_1_out[1], in_2[1]);
  not not_3 (not_1_out[2], in_2[2]);
  not not_4 (not_1_out[3], in_2[3]);
  not not_5 (not_1_out[4], in_2[4]);
  not not_6 (not_1_out[5], in_2[5]);
  not not_7 (not_1_out[6], in_2[6]);
  not not_8 (not_1_out[7], in_2[7]);
  not not_9 (not_1_out[8], in_2[8]);
  not not_10 (not_1_out[9], in_2[9]);
  not not_11 (not_1_out[10], in_2[10]);
  not not_12 (not_1_out[11], in_2[11]);
  not not_13 (not_1_out[12], in_2[12]);
  not not_14 (not_1_out[13], in_2[13]);
  not not_15 (not_1_out[14], in_2[14]);
  not not_16 (not_1_out[15], in_2[15]);
  not not_17 (not_1_out[16], in_2[16]);
  not not_18 (not_1_out[17], in_2[17]);
  _2x1_MUX u_2x1_mux_1 (.S0(in_2[18]), .in_2(in_2), .in_3(n19_bit_adder_and_subtractor_1_sum), .out_4(out_3));
  _19_bit_Adder_and_subtractor u_19_bit_adder_and_subtractor_1 (
    .Cin(in_1), .A(19'h1), .B({in_2[18], not_1_out}), .Sum(n19_bit_adder_and_subtractor_1_sum));  // open: Carry, Overflow

  // Notes on the sheet:
  //   Nurul Absar Shadik
endmodule

module _2_bit_PLR (
  input  LOAD,
  input  [1:0] in_2,
  input  CLK,
  input  CLR,
  output [1:0] out_5
);

  wire and_1_out, and_2_out, and_3_out, and_4_out, not_1_out, not_2_out;

  not not_1 (not_1_out, in_2[1]);
  not not_2 (not_2_out, in_2[0]);
  and and_1 (and_1_out, in_2[0], LOAD);
  and and_2 (and_2_out, not_2_out, LOAD);
  and and_3 (and_3_out, in_2[1], LOAD);
  and and_4 (and_4_out, not_1_out, LOAD);
  J_K_Flip_Flop j_k_ff_1 (.J(and_1_out), .clk(CLK), .K(and_2_out), .Q(out_5[0]), .reset(CLR));  // open: Qn, preset, en
  J_K_Flip_Flop j_k_ff_2 (.J(and_3_out), .clk(CLK), .K(and_4_out), .Q(out_5[1]), .reset(CLR));  // open: Qn, preset, en

  // Notes on the sheet:
  //   Nurul Absar Shadik
endmodule

module IR (
  input  LOAD,
  input  [3:0] Datain,
  input  CLK,
  input  CLR,
  output [3:0] out_5
);

  wire and_1_out, and_2_out, and_3_out, and_4_out, and_5_out, and_6_out, and_7_out, and_8_out, not_1_out,
       not_2_out, not_3_out, not_4_out;

  not not_1 (not_1_out, Datain[0]);
  not not_2 (not_2_out, Datain[1]);
  not not_3 (not_3_out, Datain[2]);
  not not_4 (not_4_out, Datain[3]);
  and and_1 (and_1_out, Datain[0], LOAD);
  and and_2 (and_2_out, not_1_out, LOAD);
  and and_3 (and_3_out, Datain[1], LOAD);
  and and_4 (and_4_out, not_2_out, LOAD);
  and and_5 (and_5_out, not_3_out, LOAD);
  and and_6 (and_6_out, Datain[3], LOAD);
  and and_7 (and_7_out, Datain[2], LOAD);
  and and_8 (and_8_out, not_4_out, LOAD);
  J_K_Flip_Flop j_k_ff_1 (.J(and_1_out), .clk(CLK), .K(and_2_out), .Q(out_5[0]), .reset(CLR));  // open: Qn, preset, en
  J_K_Flip_Flop j_k_ff_2 (.J(and_3_out), .clk(CLK), .K(and_4_out), .Q(out_5[1]), .reset(CLR));  // open: Qn, preset, en
  J_K_Flip_Flop j_k_ff_3 (.J(and_7_out), .clk(CLK), .K(and_5_out), .Q(out_5[2]), .reset(CLR));  // open: Qn, preset, en
  J_K_Flip_Flop j_k_ff_4 (.J(and_6_out), .clk(CLK), .K(and_8_out), .Q(out_5[3]), .reset(CLR));  // open: Qn, preset, en

  // Notes on the sheet:
  //   Nurul Absar Shadik
endmodule

module _3_BIT_PLR (
  input  LOAD,
  input  [2:0] in_2,
  input  CLK,
  input  CLR,
  output [2:0] out_5
);

  wire and_1_out, and_2_out, and_3_out, and_4_out, and_5_out, and_6_out, not_1_out, not_2_out, not_3_out;

  not not_1 (not_1_out, in_2[0]);
  not not_2 (not_2_out, in_2[1]);
  not not_3 (not_3_out, in_2[2]);
  and and_1 (and_1_out, in_2[0], LOAD);
  and and_2 (and_2_out, not_1_out, LOAD);
  and and_3 (and_3_out, in_2[1], LOAD);
  and and_4 (and_4_out, not_2_out, LOAD);
  and and_5 (and_5_out, in_2[2], LOAD);
  and and_6 (and_6_out, not_3_out, LOAD);
  J_K_Flip_Flop j_k_ff_1 (.J(and_1_out), .clk(CLK), .K(and_2_out), .Q(out_5[0]), .reset(CLR));  // open: Qn, preset, en
  J_K_Flip_Flop j_k_ff_2 (.J(and_3_out), .clk(CLK), .K(and_4_out), .Q(out_5[1]), .reset(CLR));  // open: Qn, preset, en
  J_K_Flip_Flop j_k_ff_3 (.J(and_5_out), .clk(CLK), .K(and_6_out), .Q(out_5[2]), .reset(CLR));  // open: Qn, preset, en

  // Notes on the sheet:
  //   Nurul Absar Shadik
endmodule

module MBR (
  input  Count,
  input  LOAD,
  input  [18:0] in_3,
  input  clk,
  input  clr,
  output [18:0] out_6
);

  wire clock_1_out, n4_bit_cpl_1_cout, n4_bit_cpl_2_cout, n4_bit_cpl_3_cout, n4_bit_cpl_4_cout;

  Clock clock_1 (.out(clock_1_out));
  _4_bit_CPL u_4_bit_cpl_1 (
    .Cin(Count), .count(Count), .LOAD(LOAD), .Data_prime(in_3[3:0]), .clk(clock_1_out), .clr(clr),
    .out_7(out_6[3:0]), .Cout(n4_bit_cpl_1_cout));
  _4_bit_CPL u_4_bit_cpl_2 (
    .Cin(n4_bit_cpl_1_cout), .count(Count), .LOAD(LOAD), .Data_prime(in_3[7:4]), .clk(clock_1_out),
    .clr(clr), .out_7(out_6[7:4]), .Cout(n4_bit_cpl_2_cout));
  _4_bit_CPL u_4_bit_cpl_3 (
    .Cin(n4_bit_cpl_2_cout), .count(Count), .LOAD(LOAD), .Data_prime(in_3[11:8]), .clk(clock_1_out),
    .clr(clr), .out_7(out_6[11:8]), .Cout(n4_bit_cpl_3_cout));
  _4_bit_CPL u_4_bit_cpl_4 (
    .Cin(n4_bit_cpl_3_cout), .count(Count), .LOAD(LOAD), .Data_prime(in_3[15:12]), .clk(clock_1_out),
    .clr(clr), .out_7(out_6[15:12]), .Cout(n4_bit_cpl_4_cout));
  _3_bit_CPL u_3_bit_cpl_1 (
    .Cin(n4_bit_cpl_4_cout), .count(Count), .LOAD(LOAD), .in_4(in_3[18:16]), .CLK(clock_1_out), .CLR(clr),
    .out_7(out_6[18:16]));  // open: Cout
  // Probe on out_6

  // Notes on the sheet:
  //   Nurul Absar Shadik
endmodule

module _2_bit_CPL (
  input  Cin,
  input  count,
  input  LOAD,
  input  [1:0] in_4,
  input  CLR,
  input  CLK,
  output [1:0] out_7
);

  wire and_1_out, and_2_out, and_3_out, and_4_out, and_5_out, and_6_out, and_7_out, not_1_out, not_2_out,
       not_3_out, or_1_out, or_2_out, or_3_out, or_4_out;

  not not_1 (not_1_out, LOAD);
  and and_1 (and_1_out, count, not_1_out);
  not not_2 (not_2_out, in_4[0]);
  not not_3 (not_3_out, in_4[1]);
  and and_2 (and_2_out, LOAD, in_4[0]);
  and and_3 (and_3_out, LOAD, not_2_out);
  and and_4 (and_4_out, LOAD, in_4[1]);
  and and_5 (and_5_out, LOAD, not_3_out);
  and and_6 (and_6_out, and_1_out, Cin);
  and and_7 (and_7_out, and_1_out, Cin, out_7[0]);
  or or_1 (or_1_out, and_2_out, and_6_out);
  or or_2 (or_2_out, and_6_out, and_3_out);
  or or_3 (or_3_out, and_4_out, and_7_out);
  or or_4 (or_4_out, and_7_out, and_5_out);
  J_K_Flip_Flop j_k_ff_1 (.J(or_1_out), .clk(CLK), .K(or_2_out), .Q(out_7[0]), .reset(CLR));  // open: Qn, preset, en
  J_K_Flip_Flop j_k_ff_2 (.J(or_3_out), .clk(CLK), .K(or_4_out), .Q(out_7[1]), .reset(CLR));  // open: Qn, preset, en

  // Notes on the sheet:
  //   Nurul Absar Shadik
endmodule

module _3_bit_CPL (
  input  Cin,
  input  count,
  input  LOAD,
  input  [2:0] in_4,
  input  CLK,
  input  CLR,
  output [2:0] out_7,
  output Cout
);

  wire and_1_out, and_2_out, and_3_out, and_4_out, and_5_out, and_6_out, and_7_out, and_8_out, and_9_out,
       and_10_out, not_1_out, not_2_out, not_3_out, not_4_out, or_1_out, or_2_out, or_3_out, or_4_out,
       or_5_out, or_6_out;

  not not_1 (not_1_out, LOAD);
  and and_1 (and_1_out, count, not_1_out);
  not not_2 (not_2_out, in_4[0]);
  not not_3 (not_3_out, in_4[1]);
  not not_4 (not_4_out, in_4[2]);
  and and_2 (and_2_out, LOAD, in_4[0]);
  and and_3 (and_3_out, LOAD, not_2_out);
  and and_4 (and_4_out, LOAD, in_4[1]);
  and and_5 (and_5_out, LOAD, not_3_out);
  and and_6 (and_6_out, not_4_out, LOAD);
  and and_7 (and_7_out, in_4[2], LOAD);
  and and_8 (and_8_out, and_1_out, Cin);
  and and_9 (and_9_out, and_1_out, Cin, out_7[0]);
  and and_10 (and_10_out, out_7[0], and_1_out, Cin, out_7[1]);
  or or_1 (or_1_out, and_2_out, and_8_out);
  or or_2 (or_2_out, and_8_out, and_3_out);
  or or_3 (or_3_out, and_4_out, and_9_out);
  or or_4 (or_4_out, and_9_out, and_5_out);
  or or_5 (or_5_out, and_7_out, and_10_out);
  or or_6 (or_6_out, and_10_out, and_6_out);
  J_K_Flip_Flop j_k_ff_1 (.J(or_1_out), .clk(CLK), .K(or_2_out), .Q(out_7[0]), .reset(CLR));  // open: Qn, preset, en
  J_K_Flip_Flop j_k_ff_2 (.J(or_3_out), .clk(CLK), .K(or_4_out), .Q(out_7[1]), .reset(CLR));  // open: Qn, preset, en
  J_K_Flip_Flop j_k_ff_3 (.J(or_5_out), .clk(CLK), .K(or_6_out), .Q(out_7[2]), .reset(CLR));  // open: Qn, preset, en
  and and_11 (Cout, out_7[0], and_1_out, Cin, out_7[1], out_7[2]);

  // Notes on the sheet:
  //   Nurul Absar Shadik
endmodule

module _4_bit_CPL (
  input  Cin,
  input  count,
  input  LOAD,
  input  [3:0] Data_prime,
  input  clk,
  input  clr,
  output [3:0] out_7,
  output Cout
);

  wire and_1_out, and_2_out, and_3_out, and_4_out, and_5_out, and_6_out, and_7_out, and_8_out, and_9_out,
       and_10_out, and_11_out, and_12_out, and_13_out, clock_1_out, not_1_out, not_2_out, not_3_out,
       not_4_out, not_5_out, or_1_out, or_2_out, or_3_out, or_4_out, or_5_out, or_6_out, or_7_out, or_8_out;

  and and_1 (and_1_out, count, not_1_out);
  not not_1 (not_1_out, LOAD);
  Clock clock_1 (.out(clock_1_out));
  not not_2 (not_2_out, Data_prime[0]);
  not not_3 (not_3_out, Data_prime[1]);
  not not_4 (not_4_out, Data_prime[2]);
  not not_5 (not_5_out, Data_prime[3]);
  and and_2 (and_2_out, LOAD, Data_prime[0]);
  and and_3 (and_3_out, LOAD, not_2_out);
  and and_4 (and_4_out, LOAD, Data_prime[1]);
  and and_5 (and_5_out, LOAD, not_3_out);
  and and_6 (and_6_out, LOAD, Data_prime[2]);
  and and_7 (and_7_out, LOAD, not_4_out);
  and and_8 (and_8_out, LOAD, Data_prime[3]);
  and and_9 (and_9_out, LOAD, not_5_out);
  and and_10 (and_10_out, and_1_out, Cin);
  and and_11 (and_11_out, and_1_out, Cin, out_7[0]);
  and and_12 (and_12_out, out_7[0], Cin, out_7[1], and_1_out);
  and and_13 (and_13_out, and_1_out, out_7[0], Cin, out_7[1], out_7[2]);
  or or_1 (or_1_out, and_2_out, and_10_out);
  or or_2 (or_2_out, and_10_out, and_3_out);
  or or_3 (or_3_out, and_4_out, and_11_out);
  or or_4 (or_4_out, and_11_out, and_5_out);
  or or_5 (or_5_out, and_6_out, and_12_out);
  or or_6 (or_6_out, and_12_out, and_7_out);
  or or_7 (or_7_out, and_8_out, and_13_out);
  or or_8 (or_8_out, and_13_out, and_9_out);
  J_K_Flip_Flop j_k_ff_1 (
    .J(or_1_out), .clk(clock_1_out), .K(or_2_out), .Q(out_7[0]), .reset(clr));  // open: Qn, preset, en
  J_K_Flip_Flop j_k_ff_2 (
    .J(or_3_out), .clk(clock_1_out), .K(or_4_out), .Q(out_7[1]), .reset(clr));  // open: Qn, preset, en
  J_K_Flip_Flop j_k_ff_3 (
    .J(or_5_out), .clk(clock_1_out), .K(or_6_out), .Q(out_7[2]), .reset(clr));  // open: Qn, preset, en
  J_K_Flip_Flop j_k_ff_4 (
    .J(or_7_out), .clk(clock_1_out), .K(or_8_out), .Q(out_7[3]), .reset(clr));  // open: Qn, preset, en
  and and_14 (Cout, out_7[2], out_7[0], out_7[1], out_7[3], and_1_out, Cin);
  // Probe on out_7

  // Notes on the sheet:
  //   Nurul Absar Shadik
endmodule

module MAR (
  input  load,
  input  [4:0] Data_in,
  input  clk,
  input  clr,
  output [4:0] out_5
);

  wire CLK_out;

  Clock u_CLK (.out(CLK_out));
  _3_BIT_PLR u_3_bit_plr_1 (.in_2(Data_in[2:0]), .CLK(CLK_out), .CLR(clr), .LOAD(load), .out_5(out_5[2:0]));
  _2_bit_PLR u_2_bit_plr_1 (.in_2(Data_in[4:3]), .CLK(CLK_out), .CLR(clr), .LOAD(load), .out_5(out_5[4:3]));

  // Notes on the sheet:
  //   Nurul Absar Shadik
endmodule

// PC
module Program_Counter (
  input  lOAD,
  input  Count,
  input  [4:0] in_3,
  input  CLK,
  input  CLR,
  output [4:0] out_6
);

  wire CLK_out, n3_bit_cpl_1_cout;

  Clock u_CLK (.out(CLK_out));
  _3_bit_CPL u_3_bit_cpl_1 (
    .Cin(Count), .count(Count), .LOAD(lOAD), .in_4(in_3[2:0]), .CLK(CLK_out), .CLR(CLR), .out_7(out_6[2:0]),
    .Cout(n3_bit_cpl_1_cout));
  _2_bit_CPL u_2_bit_cpl_1 (
    .Cin(n3_bit_cpl_1_cout), .count(Count), .LOAD(lOAD), .in_4(in_3[4:3]), .CLR(CLR), .CLK(CLK_out),
    .out_7(out_6[4:3]));
  // Probe on out_6

  // Notes on the sheet:
  //   Nurul Absar Shadik
endmodule

// AC
module Accumulator (
  input  load,
  input  [18:0] DataIn,
  input  Clk,
  input  in_4,
  output [18:0] out_5
);

  wire CLK_out;

  Clock u_CLK (.out(CLK_out));
  IR ir_1 (.Datain(DataIn[3:0]), .CLK(CLK_out), .CLR(in_4), .LOAD(load), .out_5(out_5[3:0]));
  IR ir_2 (.Datain(DataIn[7:4]), .CLK(CLK_out), .CLR(in_4), .LOAD(load), .out_5(out_5[7:4]));
  IR ir_3 (.Datain(DataIn[11:8]), .CLK(CLK_out), .CLR(in_4), .LOAD(load), .out_5(out_5[11:8]));
  IR ir_4 (.Datain(DataIn[15:12]), .CLK(CLK_out), .CLR(in_4), .LOAD(load), .out_5(out_5[15:12]));
  _3_BIT_PLR u_3_bit_plr_1 (.in_2(DataIn[18:16]), .CLK(CLK_out), .CLR(in_4), .LOAD(load), .out_5(out_5[18:16]));

  // Notes on the sheet:
  //   Nurul Absar Shadik
endmodule

module Booths_Algo (
  input  in_1,
  input  [18:0] M,
  input  [18:0] Q,
  input  in_4,
  output [18:0] out_5,
  output [18:0] out_6
);

  wire clock_1_out, controller_1_ci_a_q_1, controller_1_dec_cnt, controller_1_load_a,
       controller_1_load_m_q_cnt, controller_1_shr, or_1_out, shift_register_1_out, shift_register_3_out,
       shift_register_4_q0;
  wire [1:0] controller_1_c0;
  wire [4:0] counter_1_q;
  wire [18:0] n2_s_complement_1_out_3, n2_s_complement_2_out_3, n19_bit_alu_1_result, shift_register_2_q18;

  Clock clock_1 (.out(clock_1_out));
  Controller controller_1 (
    .CLK(clock_1_out), .RESET(in_4), .Q0(out_6[0]), .Q_1(shift_register_4_q0), .count(counter_1_q),
    .Ci_A_Q_1(controller_1_ci_a_q_1), .Load_M_Q_cnt(controller_1_load_m_q_cnt), .LOAD_A(controller_1_load_a),
    .C0(controller_1_c0[0]), .C1(controller_1_c0[1]), .Shr(controller_1_shr), .Dec_cnt(controller_1_dec_cnt));
  or or_1 (or_1_out, controller_1_load_m_q_cnt, controller_1_dec_cnt);
  Counter #(.width(5), .max('h14)) counter_1 (
    .load(or_1_out), .D(5'b10011), .count(controller_1_dec_cnt), .Q(counter_1_q), .clk(clock_1_out));  // open: carry, clr
  Shift_Register #(.length(19)) shift_register_1 (
    .shift(controller_1_shr), .in(out_5[18]), .clk(clock_1_out), .out(shift_register_1_out),
    .load(controller_1_load_a), .clr(controller_1_ci_a_q_1), .d0(n19_bit_alu_1_result[18]), .q0(out_5[18]),
    .d1(n19_bit_alu_1_result[17]), .q1(out_5[17]), .d2(n19_bit_alu_1_result[16]), .q2(out_5[16]),
    .d3(n19_bit_alu_1_result[15]), .q3(out_5[15]), .d4(n19_bit_alu_1_result[14]), .q4(out_5[14]),
    .d5(n19_bit_alu_1_result[13]), .q5(out_5[13]), .d6(n19_bit_alu_1_result[12]), .q6(out_5[12]),
    .d7(n19_bit_alu_1_result[11]), .q7(out_5[11]), .d8(n19_bit_alu_1_result[10]), .q8(out_5[10]),
    .d9(n19_bit_alu_1_result[9]), .q9(out_5[9]), .d10(n19_bit_alu_1_result[8]), .q10(out_5[8]),
    .d11(n19_bit_alu_1_result[7]), .q11(out_5[7]), .d12(n19_bit_alu_1_result[6]), .q12(out_5[6]),
    .d13(n19_bit_alu_1_result[5]), .q13(out_5[5]), .d14(n19_bit_alu_1_result[4]), .q14(out_5[4]),
    .d15(n19_bit_alu_1_result[3]), .q15(out_5[3]), .d16(n19_bit_alu_1_result[2]), .q16(out_5[2]),
    .d17(n19_bit_alu_1_result[1]), .q17(out_5[1]), .d18(n19_bit_alu_1_result[0]), .q18(out_5[0]));
  _2_s_complement u_2_s_complement_1 (.in_1(in_1), .in_2(M), .out_3(n2_s_complement_1_out_3));
  _2_s_complement u_2_s_complement_2 (.in_1(in_1), .in_2(Q), .out_3(n2_s_complement_2_out_3));
  _19_BIT_ALU u_19_bit_alu_1 (
    .Control(controller_1_c0), .A(out_5), .B(shift_register_2_q18), .result(n19_bit_alu_1_result));
  Shift_Register #(.length(19)) shift_register_2 (
    .shift(1'b0), .clk(clock_1_out), .load(controller_1_load_m_q_cnt), .d0(n2_s_complement_1_out_3[18]),
    .q0(shift_register_2_q18[18]), .d1(n2_s_complement_1_out_3[17]), .q1(shift_register_2_q18[17]),
    .d2(n2_s_complement_1_out_3[16]), .q2(shift_register_2_q18[16]), .d3(n2_s_complement_1_out_3[15]),
    .q3(shift_register_2_q18[15]), .d4(n2_s_complement_1_out_3[14]), .q4(shift_register_2_q18[14]),
    .d5(n2_s_complement_1_out_3[13]), .q5(shift_register_2_q18[13]), .d6(n2_s_complement_1_out_3[12]),
    .q6(shift_register_2_q18[12]), .d7(n2_s_complement_1_out_3[11]), .q7(shift_register_2_q18[11]),
    .d8(n2_s_complement_1_out_3[10]), .q8(shift_register_2_q18[10]), .d9(n2_s_complement_1_out_3[9]),
    .q9(shift_register_2_q18[9]), .d10(n2_s_complement_1_out_3[8]), .q10(shift_register_2_q18[8]),
    .d11(n2_s_complement_1_out_3[7]), .q11(shift_register_2_q18[7]), .d12(n2_s_complement_1_out_3[6]),
    .q12(shift_register_2_q18[6]), .d13(n2_s_complement_1_out_3[5]), .q13(shift_register_2_q18[5]),
    .d14(n2_s_complement_1_out_3[4]), .q14(shift_register_2_q18[4]), .d15(n2_s_complement_1_out_3[3]),
    .q15(shift_register_2_q18[3]), .d16(n2_s_complement_1_out_3[2]), .q16(shift_register_2_q18[2]),
    .d17(n2_s_complement_1_out_3[1]), .q17(shift_register_2_q18[1]), .d18(n2_s_complement_1_out_3[0]),
    .q18(shift_register_2_q18[0]));  // open: in, out, clr
  Shift_Register #(.length(19)) shift_register_3 (
    .shift(controller_1_shr), .in(shift_register_1_out), .clk(clock_1_out), .out(shift_register_3_out),
    .load(controller_1_load_m_q_cnt), .d0(n2_s_complement_2_out_3[18]), .q0(out_6[18]),
    .d1(n2_s_complement_2_out_3[17]), .q1(out_6[17]), .d2(n2_s_complement_2_out_3[16]), .q2(out_6[16]),
    .d3(n2_s_complement_2_out_3[15]), .q3(out_6[15]), .d4(n2_s_complement_2_out_3[14]), .q4(out_6[14]),
    .d5(n2_s_complement_2_out_3[13]), .q5(out_6[13]), .d6(n2_s_complement_2_out_3[12]), .q6(out_6[12]),
    .d7(n2_s_complement_2_out_3[11]), .q7(out_6[11]), .d8(n2_s_complement_2_out_3[10]), .q8(out_6[10]),
    .d9(n2_s_complement_2_out_3[9]), .q9(out_6[9]), .d10(n2_s_complement_2_out_3[8]), .q10(out_6[8]),
    .d11(n2_s_complement_2_out_3[7]), .q11(out_6[7]), .d12(n2_s_complement_2_out_3[6]), .q12(out_6[6]),
    .d13(n2_s_complement_2_out_3[5]), .q13(out_6[5]), .d14(n2_s_complement_2_out_3[4]), .q14(out_6[4]),
    .d15(n2_s_complement_2_out_3[3]), .q15(out_6[3]), .d16(n2_s_complement_2_out_3[2]), .q16(out_6[2]),
    .d17(n2_s_complement_2_out_3[1]), .q17(out_6[1]), .d18(n2_s_complement_2_out_3[0]), .q18(out_6[0]));  // open: clr
  Shift_Register #(.length(1)) shift_register_4 (
    .shift(controller_1_shr), .in(shift_register_3_out), .clk(clock_1_out), .clr(controller_1_ci_a_q_1),
    .q0(shift_register_4_q0));  // open: out, load, d0

  // Notes on the sheet:
  //   2207065
  //   Nurul Absar Shadik
  //   RESULT
endmodule
