// Logisim project Computer.circ as structural Verilog: 4 circuits, main circuit main
module main (
  input  Reset,
  output [18:0] out_2
);

  wire AC__MBR, AC_t, Bz, Clock, clock_1_out, F__0, F__1, IR__MBR_OP, j_k_ff_1_q, j_k_ff_1_qn, LFS, Load_A,
       LOAD_B, Load_C, M__MBR, MAR__MBR_ADD, MAR__PC, MBR__AC, MBR__M, MBR__MBR_1, MBR__PC, not_1_out, ON,
       or_3_out, PC__MAR, PC__MBR_ADD, PC__PC_1, RIGHT_SHIFT, S;
  wire [1:0] alu_control_1_c0, priority_encoder_1_out;
  wire [3:0] IR;
  wire [4:0] MAR, multiplexer_1_out, multiplexer_2_out, PC;
  wire [9:0] undriven;
  wire [18:0] AC_IN, M0UT, MBR, multiplexer_3_out, multiplexer_4_out, multiplexer_5_out, RESULT;

  Clock clock_1 (.out(clock_1_out));
  or or_1 (Load_C, PC__MBR_ADD, PC__MAR);
  Multiplexer #(.width(5)) multiplexer_1 (
    .in0(MBR[4:0]), .in1(PC), .out(multiplexer_1_out), .sel(MAR__PC));  // open: en
  and and_1 (Clock, clock_1_out, S);
  D_Flip_Flop u_S (.clk(Clock), .D(ON), .Q(S), .reset(Reset));  // open: Qn, preset, en
  or or_2 (Load_A, MAR__PC, MAR__MBR_ADD);
  Multiplexer #(.width(5)) multiplexer_2 (
    .in0(MAR), .in1(MBR[4:0]), .out(multiplexer_2_out), .sel(PC__MBR_ADD));  // open: en
  MAR mar_1 (.Data_in(multiplexer_1_out), .clk(Clock), .clr(Reset), .load(Load_A), .out_5(MAR));
  Program_Counter program_counter_1 (
    .Count(PC__PC_1), .in_3(multiplexer_2_out), .CLK(Clock), .CLR(Reset), .lOAD(Load_C), .out_6(PC));
  J_K_Flip_Flop j_k_ff_1 (
    .J(F__1), .clk(Clock), .K(F__0), .Q(j_k_ff_1_q), .Qn(j_k_ff_1_qn), .reset(Reset));  // open: preset, en
  ALU_CONTROL alu_control_1 (.IR(IR), .C0(alu_control_1_c0[0]), .C1(alu_control_1_c0[1]));
  not not_1 (not_1_out, Clock);
  _19_BIT_ALU u_19_bit_alu_1 (.Control(alu_control_1_c0), .A(out_2), .B(MBR), .result(RESULT));
  Multiplexer #(.width(19)) multiplexer_3 (.in0(MBR), .in1(RESULT), .out(multiplexer_3_out), .sel(AC_t));  // open: en
  Shift_Register #(.length(19)) shift_register_1 (
    .shift(RIGHT_SHIFT), .in(1'b0), .clk(not_1_out), .load(LFS), .clr(Reset), .d0(out_2[18]), .q0(AC_IN[18]),
    .d1(out_2[17]), .q1(AC_IN[17]), .d2(out_2[16]), .q2(AC_IN[16]), .d3(out_2[15]), .q3(AC_IN[15]),
    .d4(out_2[14]), .q4(AC_IN[14]), .d5(out_2[13]), .q5(AC_IN[13]), .d6(out_2[12]), .q6(AC_IN[12]),
    .d7(out_2[11]), .q7(AC_IN[11]), .d8(out_2[10]), .q8(AC_IN[10]), .d9(out_2[9]), .q9(AC_IN[9]),
    .d10(out_2[8]), .q10(AC_IN[8]), .d11(out_2[7]), .q11(AC_IN[7]), .d12(out_2[6]), .q12(AC_IN[6]),
    .d13(out_2[5]), .q13(AC_IN[5]), .d14(out_2[4]), .q14(AC_IN[4]), .d15(out_2[3]), .q15(AC_IN[3]),
    .d16(out_2[2]), .q16(AC_IN[2]), .d17(out_2[1]), .q17(AC_IN[1]), .d18(out_2[0]), .q18(AC_IN[0]));  // open: out
  RAM #(.addrWidth(5), .dataWidth(19), .bus("separate")) ram_1 (
    .addr(MAR), .din(MBR), .data(M0UT), .str(M__MBR), .clk(Clock), .ld(MBR__M));  // open: sel, clr
  or or_3 (or_3_out, AC__MBR, RIGHT_SHIFT, AC_t);
  Multiplexer #(.width(19), .enable("false")) multiplexer_4 (
    .in0(multiplexer_3_out), .in1(AC_IN), .out(multiplexer_4_out), .sel(RIGHT_SHIFT));
  Control_Unit control_unit_1 (
    .Clock(Clock), .Reset(Reset), .F(j_k_ff_1_q), .F_prime(j_k_ff_1_qn), .Bz(Bz), .S(S), .IR(IR),
    .out_25(LFS), .MAR__PC(MAR__PC), .MBR__M(MBR__M), .PC__PC_1(PC__PC_1), .IR__MBR_OP(IR__MBR_OP),
    .F__1(F__1), .PC__MBR_ADD(PC__MBR_ADD), .MAR__MBR_ADD(MAR__MBR_ADD), .F__0(F__0), .AC(AC_t),
    .MBR__AC(MBR__AC), .M__MBR(M__MBR), .MBR__MBR_1(MBR__MBR_1), .AC__MBR(AC__MBR), .PC__MAR(PC__MAR),
    .MBR__PC(MBR__PC), .ON(ON), .RIGHT_SHIFT(RIGHT_SHIFT));
  Accumulator accumulator_1 (.DataIn(multiplexer_4_out), .Clk(Clock), .in_4(Reset), .load(or_3_out), .out_5(out_2));
  or or_4 (LOAD_B, MBR__PC, MBR__AC, MBR__M);
  Multiplexer #(.select(2), .width(19)) multiplexer_5 (
    .in0(M0UT), .in1(out_2), .in2({4'b0101, undriven, PC}), .out(multiplexer_5_out),
    .sel(priority_encoder_1_out));  // open: in3, en
  Priority_Encoder #(.select(2)) priority_encoder_1 (
    .in0(MBR__M), .in1(MBR__AC), .in2(MBR__PC), .out(priority_encoder_1_out));  // open: in3
  IR ir_1 (.Datain(MBR[18:15]), .CLK(Clock), .CLR(Reset), .LOAD(IR__MBR_OP), .out_5(IR));
  MBR mbr_1 (.Count(MBR__MBR_1), .LOAD(LOAD_B), .in_3(multiplexer_5_out), .clk(Clock), .clr(Reset), .out_6(MBR));
  Bz bz_1 (.in_1(MBR), .out_2(Bz));

  // Other names for the same wires on the sheet: AC[18:0] = out_2; MBR_ADD[4:0] = MBR[4:0]; MBR_OP[3:0] = MBR[18:15]

  // Notes on the sheet:
  //   MEMORY ADDRESS  REGISTER
  //   PROGRAM COUNTER
  //   2207065
  //   ALU
  //   Control Unit
  //   Tiny Computer
  //   ACCUMULATOR
  //   MEMORY BUFFER REGISTER
  //   INSTRUCTION REGISTER
endmodule

module Control_Unit (
  input  Clock,
  input  Reset,
  input  F,
  input  F_prime,
  input  Bz,
  input  S,
  input  [3:0] IR,
  output MAR__PC,
  output MBR__M,
  output PC__PC_1,
  output IR__MBR_OP,
  output F__1,
  output PC__MBR_ADD,
  output MAR__MBR_ADD,
  output F__0,
  output AC,
  output MBR__AC,
  output M__MBR,
  output MBR__MBR_1,
  output AC__MBR,
  output PC__MAR,
  output MBR__PC,
  output ON,
  output RIGHT_SHIFT,
  output out_25
);

  wire _21, _22, _23, _24, _25, _26, and_4_out, and_6_out, and_9_out, and_13_out, and_17_out, and_19_out,
       or_1_out, or_2_out, or_6_out, or_8_out, q0, q1, q2, q3, q4, q5, q6, q7, q8, q9, q10, q11, q12, T0, T2,
       T3;
  wire [1:0] counter_1_q;

  Counter #(.width(2), .max('h3)) counter_1 (
    .load(1'b0), .Q(counter_1_q), .clk(Clock), .clr(Reset));  // open: D, count, carry
  Decoder #(.select(2)) decoder_1 (.out0(T0), .out1(out_25), .out2(T2), .out3(T3), .sel(counter_1_q));  // open: en
  and and_1 (F__0, F, T3);
  or or_1 (or_1_out, q1, q0, q9, q8);
  Decoder #(.select(4)) decoder_2 (
    .out0(q0), .out1(q1), .out2(q2), .out3(q3), .out4(q4), .out5(q5), .out6(q6), .out7(q7), .out8(q8),
    .out9(q9), .out10(q10), .out11(q11), .out12(q12), .sel(IR));  // open: out13, out14, out15, en
  and and_2 (MAR__MBR_ADD, F, T0);
  or or_2 (or_2_out, q0, q1, q2, q3, q9, q7, q8, q11);
  and and_3 (MBR__AC, F, q2, T2);
  and and_4 (and_4_out, F, q2, T3);
  and and_5 (_23, F, q3, T3, Bz);
  and and_6 (and_6_out, F, q7, T2);
  and and_7 (MBR__PC, F, q4, T2);
  and and_8 (_22, F, q4, T3);
  and and_9 (and_9_out, q6, T3);
  and and_10 (_24, F, q11, T2);
  and and_11 (_26, F, q11, T3);
  and and_12 (RIGHT_SHIFT, F, T2, q12);
  and and_13 (and_13_out, F, q3, T2);
  and and_14 (_25, F, q3, T3);
  or or_3 (AC__MBR, and_6_out, _26);
  not not_1 (ON, and_9_out);
  and and_15 (AC, F, or_1_out, T3);
  and and_16 (_21, F, or_2_out, out_25);
  or or_4 (M__MBR, and_4_out, _26, _25, _22);
  or or_5 (MBR__MBR_1, and_13_out, _24);
  and and_17 (and_17_out, F_prime, out_25);
  and and_18 (MAR__PC, F_prime, T0);
  and and_19 (and_19_out, F_prime, out_25);
  and and_20 (IR__MBR_OP, F_prime, T2);
  or or_6 (or_6_out, q0, q1, q2, q3, q11, q4, q7, q8, q9);
  and and_21 (PC__MBR_ADD, q5, T3);
  or or_7 (MBR__M, and_17_out, _21);
  or or_8 (or_8_out, q12, or_6_out);
  or or_9 (PC__PC_1, and_19_out, _22, _23);
  and and_22 (F__1, F_prime, or_8_out, T3);

  assign PC__MAR = MBR__PC;

  // Other names for the same wires on the sheet: T1 = out_25

  // Notes on the sheet:
  //   Time sequence
  //   Execution Cyle
  //   2207065
  //   Fetch Cycle
endmodule

module Bz (
  input  [18:0] in_1,
  output out_2
);

  wire not_1_out, or_1_out;

  not not_1 (not_1_out, in_1[0]);
  or or_1 (or_1_out, not_1_out, in_1[1], in_1[2], in_1[3], in_1[4], in_1[5], in_1[6], in_1[7], in_1[8], in_1[9], in_1[10], in_1[11], in_1[12], in_1[13], in_1[14], in_1[15], in_1[16], in_1[17], in_1[18]);
  not not_2 (out_2, or_1_out);
endmodule

module ALU_CONTROL (
  input  [3:0] IR,
  output C0,
  output C1
);

  Multiplexer #(.select(4), .width(2)) multiplexer_1 (
    .in0(2'b01), .in1(2'b10), .in2(2'b00), .in3(2'b00), .in4(2'b00), .in5(2'b00), .in6(2'b00), .in7(2'b00),
    .in8(2'b00), .in9(2'b11), .in10(2'b00), .in11(2'b00), .in12(2'b00), .in13(2'b00), .in14(2'b00),
    .in15(2'b00), .out({C1, C0}), .sel(IR));  // open: en
endmodule
